// Logisim project demonstracao_shift_register.circ as structural Verilog: 1 circuit, main circuit main
module main (
  input  in_1,
  input  in_2,
  input  in_3,
  input  in_4,
  input  in_5,
  input  in_6,
  input  in_7,
  input  in_8,
  input  in_9,
  input  in_10,
  input  in_11,
  input  in_12,
  input  in_13,
  input  in_14,
  input  in_15,
  input  in_16,
  input  in_17,
  input  in_18,
  input  in_19,
  input  in_20,
  input  in_21
);

  wire button_1_out, clock_d_out, d_ff_1_q, d_ff_2_q, d_ff_3_q, d_ff_4_q, j_k_ff_1_q, j_k_ff_2_q, j_k_ff_3_q,
       j_k_ff_4_q, not_1_out, not_2_out, not_3_out, not_4_out, reset_d_out, reset_out, shift_register_1_p14,
       shift_register_1_p15, shift_register_1_p16, shift_register_1_p17, shift_register_1_p18,
       shift_register_1_p19, shift_register_1_p20, switch_1_p1, switch_1_p2, switch_2_p2, switch_2_p4,
       switch_2_p5, switch_2_p6, switch_2_p7, switch_2_p8, switch_2_p9, switch_2_p10, switch_2_p11, undriven,
       undriven_2, undriven_3, undriven_4;

  Button button_1 (.out(button_1_out));
  Button reset (.out(reset_out));
  Clock clock_d (.out(clock_d_out));
  Button reset_d (.out(reset_d_out));
  not not_1 (not_1_out, j_k_ff_4_q);
  // Switch switch_1: pin names not known; wires that end beside it: switch_1_p1, switch_1_p2
  J_K_Flip_Flop j_k_ff_1 (
    .J(j_k_ff_4_q), .K(not_1_out), .clk(button_1_out), .Q(j_k_ff_1_q), .preset(in_1), .reset(reset_out));  // open: Qn
  D_Flip_Flop d_ff_1 (.D(d_ff_4_q), .clk(clock_d_out), .Q(d_ff_1_q), .preset(in_5), .reset(reset_d_out));  // open: Qn
  // Shift_Register shift_register_1: pin names not known; wires that end beside it: in_9, in_10, in_11, in_13, switch_1_p2, in_14, in_15, in_16, in_17, in_18, in_19, in_20, in_21, shift_register_1_p14, shift_register_1_p15, shift_register_1_p16, shift_register_1_p17, shift_register_1_p18, shift_register_1_p19, shift_register_1_p20, switch_1_p1
  LED led_1 (.in(j_k_ff_1_q));
  J_K_Flip_Flop j_k_ff_2 (
    .J(j_k_ff_1_q), .K(not_2_out), .clk(button_1_out), .Q(j_k_ff_2_q), .preset(in_2), .reset(reset_out));  // open: Qn
  not not_2 (not_2_out, j_k_ff_1_q);
  LED led_2 (.in(d_ff_1_q));
  D_Flip_Flop d_ff_2 (.D(d_ff_1_q), .clk(clock_d_out), .Q(d_ff_2_q), .preset(in_6), .reset(reset_d_out));  // open: Qn
  LED led_3 (.in(j_k_ff_2_q));
  LED led_4 (.in(j_k_ff_3_q));
  LED led_5 (.in(j_k_ff_4_q));
  LED led_6 (.in(d_ff_2_q));
  LED led_7 (.in(d_ff_3_q));
  LED led_8 (.in(shift_register_1_p14));
  J_K_Flip_Flop j_k_ff_3 (
    .J(j_k_ff_2_q), .K(not_3_out), .clk(button_1_out), .Q(j_k_ff_3_q), .preset(in_3), .reset(reset_out));  // open: Qn
  not not_3 (not_3_out, j_k_ff_2_q);
  LED led_9 (.in(d_ff_4_q));
  D_Flip_Flop d_ff_3 (.D(d_ff_2_q), .clk(clock_d_out), .Q(d_ff_3_q), .preset(in_7), .reset(reset_d_out));  // open: Qn
  LED led_10 (.in(shift_register_1_p15));
  LED led_11 (.in(shift_register_1_p16));
  LED led_12 (.in(shift_register_1_p17));
  LED led_13 (.in(shift_register_1_p18));
  LED led_14 (.in(shift_register_1_p19));
  LED led_15 (.in(shift_register_1_p20));
  J_K_Flip_Flop j_k_ff_4 (
    .J(j_k_ff_3_q), .K(not_4_out), .clk(button_1_out), .Q(j_k_ff_4_q), .preset(in_4), .reset(reset_out));  // open: Qn
  not not_4 (not_4_out, j_k_ff_3_q);
  D_Flip_Flop d_ff_4 (.D(d_ff_3_q), .clk(clock_d_out), .Q(d_ff_4_q), .preset(in_8), .reset(reset_d_out));  // open: Qn
  LED led_16 (.in(switch_1_p1));
  // Switch switch_2: pin names not known; wires that end beside it: switch_1_p1, switch_2_p2, switch_2_p2, switch_2_p4, switch_2_p5, switch_2_p6, switch_2_p7, switch_2_p8, switch_2_p9, switch_2_p10, switch_2_p11
  LED led_17 (.in(undriven));
  LED led_18 (.in(undriven));
  LED led_19 (.in(undriven_2));
  LED led_20 (.in(undriven_2));
  LED led_21 (.in(undriven_3));
  LED led_22 (.in(undriven_3));
  LED led_23 ();  // open: in
  LED led_24 ();  // open: in
  // Shift_Register shift_register_2: pin names not known; wires that end beside it: in_9, in_12, in_13
  LED led_25 (.in(undriven_4));
  LED led_26 (.in(undriven_4));
  LED led_27 ();  // open: in
  LED led_28 ();  // open: in
  LED led_29 (.in(switch_2_p4));
  LED led_30 (.in(switch_2_p5));
  LED led_31 (.in(switch_2_p8));
  LED led_32 (.in(switch_2_p6));
  LED led_33 (.in(switch_2_p7));
  LED led_34 (.in(switch_2_p9));
  LED led_35 (.in(switch_2_p10));
  LED led_36 (.in(switch_2_p11));

  // Notes on the sheet:
  //   in_1: pull=up
  //   in_5: pull=up
  //   in_2: pull=up
  //   in_6: pull=up
  //   in_3: pull=up
  //   in_7: pull=up
  //   in_4: pull=up
  //   in_8: pull=up
endmodule
